// Logisim project WITCPU.circ as structural Verilog: 10 circuits, main circuit register_group
module register_group (
  input  [15:0] in_1,
  input  Clock,
  input  [1:0] Ra,
  input  [1:0] Rd,
  input  [1:0] Rb,
  output [15:0] Ra_output,
  output [15:0] Rb_output
);

  wire demultiplexer_1_out0, demultiplexer_1_out1, demultiplexer_1_out2, demultiplexer_1_out3;
  wire [15:0] register_1_q, register_2_q, register_3_q, register_4_q;

  Demultiplexer #(.select(2)) demultiplexer_1 (
    .out0(demultiplexer_1_out0), .out1(demultiplexer_1_out1), .out2(demultiplexer_1_out2),
    .out3(demultiplexer_1_out3), .in(Clock), .sel(Rd));  // open: en
  Register #(.width(16)) register_1 (.D(in_1), .Q(register_1_q), .clk(demultiplexer_1_out0));  // open: en, clr
  Register #(.width(16)) register_2 (.D(in_1), .Q(register_2_q), .clk(demultiplexer_1_out1));  // open: en, clr
  Register #(.width(16)) register_3 (.D(in_1), .Q(register_3_q), .clk(demultiplexer_1_out2));  // open: en, clr
  Register #(.width(16)) register_4 (.D(in_1), .Q(register_4_q), .clk(demultiplexer_1_out3));  // open: en, clr
  Multiplexer #(.select(2), .width(16)) multiplexer_1 (
    .in0(register_1_q), .in1(register_2_q), .in2(register_3_q), .in3(register_4_q), .out(Ra_output), .sel(Ra));  // open: en
  Multiplexer #(.select(2), .width(16)) multiplexer_2 (
    .in0(register_1_q), .in1(register_2_q), .in2(register_3_q), .in3(register_4_q), .out(Rb_output), .sel(Rb));  // open: en
endmodule

module registers (
  input  [15:0] Rd_value,
  input  clock,
  input  [3:0] Rd,
  input  [3:0] Rx,
  input  [3:0] Ry,
  output [15:0] Rx_output,
  output [15:0] Ry_output
);

  wire demultiplexer_1_out0, demultiplexer_1_out1, demultiplexer_1_out2, demultiplexer_1_out3;
  wire [15:0] R0___R3_ra_output, R0___R3_rb_output, R4___R7_ra_output, R4___R7_rb_output, R8___Rb_ra_output,
       R8___Rb_rb_output, Rc___Rf_ra_output, Rc___Rf_rb_output;

  Demultiplexer #(.select(2)) demultiplexer_1 (
    .out0(demultiplexer_1_out0), .out1(demultiplexer_1_out1), .out2(demultiplexer_1_out2),
    .out3(demultiplexer_1_out3), .in(clock), .sel(Rd[3:2]));  // open: en
  register_group_with_r0 R0___R3 (
    .in_1(Rd_value), .Clock(demultiplexer_1_out0), .Ra(Rx[1:0]), .Rd(Rd[1:0]), .Rb(Ry[1:0]),
    .Ra_output(R0___R3_ra_output), .Rb_output(R0___R3_rb_output));
  register_group R4___R7 (
    .in_1(Rd_value), .Clock(demultiplexer_1_out1), .Ra(Rx[1:0]), .Rd(Rd[1:0]), .Rb(Ry[1:0]),
    .Ra_output(R4___R7_ra_output), .Rb_output(R4___R7_rb_output));
  register_group R8___Rb (
    .in_1(Rd_value), .Clock(demultiplexer_1_out2), .Ra(Rx[1:0]), .Rd(Rd[1:0]), .Rb(Ry[1:0]),
    .Ra_output(R8___Rb_ra_output), .Rb_output(R8___Rb_rb_output));
  register_group Rc___Rf (
    .in_1(Rd_value), .Clock(demultiplexer_1_out3), .Ra(Rx[1:0]), .Rd(Rd[1:0]), .Rb(Ry[1:0]),
    .Ra_output(Rc___Rf_ra_output), .Rb_output(Rc___Rf_rb_output));
  Multiplexer #(.select(2), .width(16)) multiplexer_1 (
    .in0(R0___R3_ra_output), .in1(R4___R7_ra_output), .in2(R8___Rb_ra_output), .in3(Rc___Rf_ra_output),
    .out(Rx_output), .sel(Rx[3:2]));  // open: en
  Multiplexer #(.select(2), .width(16)) multiplexer_2 (
    .in0(R0___R3_rb_output), .in1(R4___R7_rb_output), .in2(R8___Rb_rb_output), .in3(Rc___Rf_rb_output),
    .out(Ry_output), .sel(Ry[3:2]));  // open: en
endmodule

module register_group_with_r0 (
  input  [15:0] in_1,
  input  Clock,
  input  [1:0] Ra,
  input  [1:0] Rd,
  input  [1:0] Rb,
  output [15:0] Ra_output,
  output [15:0] Rb_output
);

  wire demultiplexer_1_out0, demultiplexer_1_out1, demultiplexer_1_out2, demultiplexer_1_out3;
  wire [15:0] register_1_q, register_2_q, register_3_q, register_4_q;

  Demultiplexer #(.select(2)) demultiplexer_1 (
    .out0(demultiplexer_1_out0), .out1(demultiplexer_1_out1), .out2(demultiplexer_1_out2),
    .out3(demultiplexer_1_out3), .in(Clock), .sel(Rd));  // open: en
  Register #(.width(16)) register_1 (.D({16{1'b0}}), .Q(register_1_q), .clk(demultiplexer_1_out0));  // open: en, clr
  Register #(.width(16)) register_2 (.D(in_1), .Q(register_2_q), .clk(demultiplexer_1_out1));  // open: en, clr
  Register #(.width(16)) register_3 (.D(in_1), .Q(register_3_q), .clk(demultiplexer_1_out2));  // open: en, clr
  Register #(.width(16)) register_4 (.D(in_1), .Q(register_4_q), .clk(demultiplexer_1_out3));  // open: en, clr
  Multiplexer #(.select(2), .width(16)) multiplexer_1 (
    .in0(register_1_q), .in1(register_2_q), .in2(register_3_q), .in3(register_4_q), .out(Ra_output), .sel(Ra));  // open: en
  Multiplexer #(.select(2), .width(16)) multiplexer_2 (
    .in0(register_1_q), .in1(register_2_q), .in2(register_3_q), .in3(register_4_q), .out(Rb_output), .sel(Rb));  // open: en
endmodule

// ALU
module alu (
  input  [15:0] data1,
  input  [15:0] data2,
  input  [3:0] opcode,
  input  [7:0] immediate,
  input  enable,
  output [15:0] out_6
);

  wire [15:0] adder_1_out, and_1_out, bit_extender_1_out, divider_1_out, multiplier_1_out, or_1_out,
       subtractor_1_out, xnor_1_out;

  Adder #(.width(16)) adder_1 (.a(data1), .b(data2), .out(adder_1_out));  // open: cin, cout
  Subtractor #(.width(16)) subtractor_1 (.a(data1), .b(data2), .out(subtractor_1_out));  // open: bin, bout
  Multiplier #(.width(16)) multiplier_1 (.a(data1), .b(data2), .out(multiplier_1_out));  // open: cin, cout
  Divider #(.width(16)) divider_1 (.a(data1), .b(data2), .out(divider_1_out));  // open: upper, rem
  assign and_1_out = data1 & data2;  // AND_Gate and_1, 16 bits wide
  assign or_1_out = data1 | data2;  // OR_Gate or_1, 16 bits wide
  assign xnor_1_out = ~(data1 ^ data2);  // XNOR_Gate xnor_1, 16 bits wide
  assign bit_extender_1_out = {{8{immediate[7]}}, immediate};  // Bit_Extender bit_extender_1
  Multiplexer #(.select(3), .width(16)) multiplexer_1 (
    .in0(adder_1_out), .in1(subtractor_1_out), .in2(multiplier_1_out), .in3(divider_1_out), .in4(and_1_out),
    .in5(or_1_out), .in6(xnor_1_out), .in7(bit_extender_1_out), .out(out_6), .sel(opcode[2:0]), .en(enable));
endmodule

module decoder (
  input  [15:0] instruction,
  output [3:0] opcode,
  output [3:0] operand_1,
  output [3:0] operand_2,
  output [3:0] operand_3,
  output [7:0] immediate
);

  Multiplexer #(.width(4)) multiplexer_1 (
    .in0(instruction[7:4]), .in1(instruction[11:8]), .out(operand_2), .sel(instruction[15]));  // open: en

  assign immediate = instruction[7:0];
  assign opcode = instruction[15:12];
  assign operand_1 = instruction[11:8];
  assign operand_3 = instruction[3:0];
endmodule

module PC (
  input  [7:0] PC_value,
  input  [7:0] immediate_value,
  input  [15:0] data_input,
  input  [3:0] opcode,
  output [7:0] PC_value_2
);

  wire and_1_out, and_2_out, comparator_1_eq, comparator_1_gt, comparator_1_lt, multiplexer_1_out, not_1_out,
       not_2_out;
  wire [7:0] adder_1_out;

  not not_1 (not_1_out, opcode[2]);
  Comparator #(.width(16)) comparator_1 (
    .a(data_input), .b({16{1'b0}}), .gt(comparator_1_gt), .eq(comparator_1_eq), .lt(comparator_1_lt));
  and and_1 (and_1_out, not_1_out, opcode[3]);
  not not_2 (not_2_out, comparator_1_eq);
  Multiplexer #(.select(2)) multiplexer_1 (
    .in0(comparator_1_eq), .in1(not_2_out), .in2(comparator_1_gt), .in3(comparator_1_lt),
    .out(multiplexer_1_out), .sel(opcode[1:0]));  // open: en
  Adder adder_1 (.a(PC_value), .b(8'h1), .out(adder_1_out));  // open: cin, cout
  Multiplexer #(.width(8)) multiplexer_2 (
    .in0(adder_1_out), .in1(immediate_value), .out(PC_value_2), .sel(and_2_out));  // open: en
  and and_2 (and_2_out, multiplexer_1_out, and_1_out);
endmodule

module RAM (
  input  [7:0] address,
  input  [15:0] value,
  input  store,
  input  enable,
  input  clock,
  input  load,
  input  clear,
  output [15:0] \output 
);

  RAM_part #(.dataWidth(16), .bus("separate")) ram_1 (
    .addr(address), .din(value), .data(\output ), .str(store), .sel(enable), .clk(clock), .ld(load),
    .clr(clear));
endmodule

// BUS
module Bus (
  input  [3:0] opcode,
  input  [7:0] immediate,
  input  [15:0] data,
  input  cycle,
  input  clock,
  output ALU_enable,
  output [7:0] RAM_address,
  output register_write,
  output RAM_read,
  output RAM_write
);

  wire and_1_out, and_2_out, and_3_out, not_1_out, not_2_out, not_3_out, not_4_out;

  not not_1 (not_1_out, opcode[1]);
  not not_2 (not_2_out, opcode[3]);
  and and_1 (and_1_out, not_2_out, cycle, clock);
  and and_2 (and_2_out, not_1_out, clock, opcode[2], opcode[3], opcode[3], cycle);
  and and_3 (and_3_out, not_1_out, opcode[3], opcode[2], cycle);
  not not_3 (not_3_out, cycle);
  not not_4 (not_4_out, opcode[3]);
  and and_4 (ALU_enable, not_4_out, cycle);
  or or_1 (register_write, and_1_out, and_2_out);
  or or_2 (RAM_read, and_3_out, not_3_out);
  and and_5 (RAM_write, opcode[1], cycle, opcode[2], opcode[3]);
  Multiplexer #(.width(8)) multiplexer_1 (
    .in0(immediate), .in1(data[7:0]), .out(RAM_address), .sel(opcode[0]));  // open: en
endmodule

module clock (
  output cycle,
  output clock
);

  wire not_1_out;

  Clock clock_1 (.out(clock));
  not not_1 (not_1_out, clock);
  T_Flip_Flop t_ff_1 (.clk(not_1_out), .T(1'b1), .Q(cycle));  // open: Qn, preset, reset, en
endmodule

module main (
);

  wire and_1_out, and_2_out, bus_1_alu_enable, bus_1_ram_read, bus_1_ram_write, bus_1_register_write,
       clock_1_out, not_1_out, t_ff_1_q;
  wire [3:0] DECODER_opcode, DECODER_operand_1, DECODER_operand_2, DECODER_operand_3;
  wire [7:0] bus_1_ram_address, DECODER_immediate, multiplexer_1_out, pc_1_pc_value_2, PC_REGISTER_q;
  wire [15:0] INSTRUCTION_REGISTER_q, ram_1_data, REGISTER_rx_output, REGISTER_ry_output;

  Clock clock_1 (.out(clock_1_out));
  not not_1 (not_1_out, clock_1_out);
  T_Flip_Flop t_ff_1 (.clk(not_1_out), .T(1'b1), .Q(t_ff_1_q));  // open: Qn, preset, reset, en
  Bus bus_1 (
    .opcode(DECODER_opcode), .immediate(DECODER_immediate), .data(REGISTER_rx_output), .cycle(t_ff_1_q),
    .clock(clock_1_out), .ALU_enable(bus_1_alu_enable), .RAM_address(bus_1_ram_address),
    .register_write(bus_1_register_write), .RAM_read(bus_1_ram_read), .RAM_write(bus_1_ram_write));
  Register #(.width(16)) INSTRUCTION_REGISTER (
    .D(ram_1_data), .Q(INSTRUCTION_REGISTER_q), .clk(and_1_out));  // open: en, clr
  and and_1 (and_1_out, ~t_ff_1_q, clock_1_out);  // AND_Gate
  and and_2 (and_2_out, t_ff_1_q, clock_1_out);
  Multiplexer #(.width(8)) multiplexer_1 (
    .in0(PC_REGISTER_q), .in1(bus_1_ram_address), .out(multiplexer_1_out), .sel(t_ff_1_q));  // open: en
  Register PC_REGISTER (.D(pc_1_pc_value_2), .Q(PC_REGISTER_q), .clk(and_2_out));  // open: en, clr
  decoder DECODER (
    .instruction(INSTRUCTION_REGISTER_q), .opcode(DECODER_opcode), .operand_1(DECODER_operand_1),
    .operand_2(DECODER_operand_2), .operand_3(DECODER_operand_3), .immediate(DECODER_immediate));
  RAM_part #(.dataWidth(16), .bus("separate")) ram_1 (
    .addr(multiplexer_1_out), .din(REGISTER_rx_output), .data(ram_1_data), .str(bus_1_ram_write),
    .clk(clock_1_out), .ld(bus_1_ram_read));  // open: sel, clr
  alu alu_1 (
    .data1(REGISTER_rx_output), .data2(REGISTER_ry_output), .opcode(DECODER_opcode),
    .immediate(DECODER_immediate), .enable(bus_1_alu_enable), .out_6(ram_1_data));
  PC pc_1 (
    .PC_value(PC_REGISTER_q), .immediate_value(DECODER_immediate), .data_input(REGISTER_rx_output),
    .opcode(DECODER_opcode), .PC_value_2(pc_1_pc_value_2));
  registers REGISTER (
    .Rd_value(ram_1_data), .clock(bus_1_register_write), .Rd(DECODER_operand_1), .Rx(DECODER_operand_2),
    .Ry(DECODER_operand_3), .Rx_output(REGISTER_rx_output), .Ry_output(REGISTER_ry_output));
endmodule
