// Logisim project lab3 asdf.circ as structural Verilog: 5 circuits, main circuit 4
module _4 (
  input  a,
  input  b,
  input  c,
  output x
);

  wire and_1_out, and_2_out, and_3_out, not_1_out, not_2_out, or_1_out, or_2_out, or_3_out;

  and and_1 (and_1_out, a, a);
  not not_1 (not_1_out, b);
  not not_2 (not_2_out, a);
  or or_1 (or_1_out, a, b);
  or or_2 (or_2_out, b, and_1_out);
  or or_3 (or_3_out, a, not_1_out);
  and and_2 (and_2_out, not_2_out, or_1_out);
  and and_3 (and_3_out, or_2_out, or_3_out);
  or or_4 (x, and_2_out, and_3_out);
endmodule

module _2 (
  input  in_1,
  input  b,
  input  c,
  output x
);

  wire nand_1_out;

  or or_1 (x, c, nand_1_out);
  nand nand_1 (nand_1_out, b, c);
endmodule

module _1 (
  input  a,
  input  b,
  input  in_3,
  input  in_4,
  output x
);

  wire nand_1_out, not_1_out, not_2_out, or_1_out, or_2_out;

  not not_1 (not_1_out, a);
  not not_2 (not_2_out, b);
  nand nand_1 (nand_1_out, a, b);
  or or_1 (or_1_out, not_1_out, b);
  or or_2 (or_2_out, not_2_out, b);
  and and_1 (x, nand_1_out, or_1_out, or_2_out);
endmodule

module _3 (
  input  a,
  input  b,
  input  c,
  input  d,
  output x
);

  wire and_1_out, and_2_out, and_3_out, and_4_out, not_1_out, or_1_out, or_2_out;

  and and_1 (and_1_out, a, d);
  and and_2 (and_2_out, a, not_1_out);
  not not_1 (not_1_out, d);
  or or_1 (or_1_out, a, c);
  or or_2 (or_2_out, and_1_out, and_2_out);
  and and_3 (and_3_out, or_1_out, or_2_out);
  and and_4 (and_4_out, a, c);
  or or_3 (x, and_3_out, and_4_out, c);
endmodule

module _5 (
  input  a,
  input  b,
  output x
);

  wire and_1_out, and_2_out, and_3_out, not_1_out, not_2_out, not_3_out, not_4_out;

  not not_1 (not_1_out, a);
  not not_2 (not_2_out, b);
  not not_3 (not_3_out, a);
  not not_4 (not_4_out, b);
  and and_1 (and_1_out, not_1_out, not_2_out);
  and and_2 (and_2_out, not_3_out, b);
  and and_3 (and_3_out, a, not_4_out);
  or or_1 (x, and_1_out, and_2_out, and_3_out);
endmodule
