// Logisim project lab3.circ as structural Verilog: 2 circuits, main circuit main
module main (
  input  a,
  input  b,
  input  c,
  input  in_4,
  output out_5
);

  Multiplexer #(.select(3)) multiplexer_1 (
    .in0(1'b0), .in1(1'b0), .in2(1'b0), .in3(1'b1), .in4(1'b0), .in5(1'b1), .in6(1'b1), .in7(1'b1),
    .out(out_5), .sel({a, b, c}));  // open: en
endmodule

module _7 (
  input  Carry_In,
  input  a,
  input  b,
  output Carry_Out,
  output out_5
);

  Multiplexer #(.select(3)) multiplexer_1 (
    .in0(1'b0), .in1(1'b0), .in2(1'b0), .in3(1'b1), .in4(1'b0), .in5(1'b1), .in6(1'b1), .in7(1'b1),
    .out(Carry_Out), .sel({Carry_In, a, b}));  // open: en
  Multiplexer #(.select(3)) multiplexer_2 (
    .in1(1'b1), .in2(1'b1), .in3(1'b0), .in4(1'b1), .in5(1'b0), .in6(1'b0), .in7(1'b1), .out(out_5),
    .sel({Carry_In, a, b}));  // open: in0, en
endmodule
