// Logisim project lab4.circ as structural Verilog: 1 circuit, main circuit main
module main (
  output out_1
);

  wire and_1_out, and_2_out, and_3_out, and_4_out, and_5_out, and_6_out, and_7_out, Cabbage_q, Cabbage_qn,
       clock_1_out, Farmer_q, Farmer_qn, Goat_q, Goat_qn, or_1_out, or_2_out, or_3_out, Wolf_q, Wolf_qn;

  Clock clock_1 (.out(clock_1_out));
  or or_1 (or_1_out, and_1_out, and_3_out, and_6_out, and_2_out);
  or or_2 (or_2_out, and_5_out, and_6_out, and_7_out);
  D_Flip_Flop Wolf (.clk(clock_1_out), .D(or_3_out), .Q(Wolf_q), .Qn(Wolf_qn));  // open: preset, en, reset
  D_Flip_Flop Goat (.clk(clock_1_out), .D(or_1_out), .Q(Goat_q), .Qn(Goat_qn));  // open: preset, en, reset
  D_Flip_Flop Cabbage (.clk(clock_1_out), .D(or_2_out), .Q(Cabbage_q), .Qn(Cabbage_qn));  // open: preset, en, reset
  T_Flip_Flop Farmer (.clk(clock_1_out), .T(1'b1), .Q(Farmer_q), .Qn(Farmer_qn));  // open: preset, reset, en
  or or_3 (or_3_out, and_2_out, and_4_out, and_6_out, and_5_out, and_7_out);
  and and_1 (and_1_out, Farmer_qn, Cabbage_qn, Goat_qn, Wolf_qn);
  and and_2 (and_2_out, Farmer_qn, Cabbage_qn, Goat_q, Wolf_qn);
  and and_3 (and_3_out, Farmer_q, Cabbage_qn, Goat_q, Wolf_qn);
  and and_4 (and_4_out, Farmer_q, Cabbage_qn, Goat_q, Wolf_q);
  and and_5 (and_5_out, Farmer_qn, Cabbage_qn, Goat_qn, Wolf_q);
  and and_6 (and_6_out, Farmer_qn, Cabbage_q, Goat_qn, Wolf_q);
  and and_7 (and_7_out, Farmer_q, Cabbage_q, Goat_qn, Wolf_q);
  and and_8 (out_1, Wolf_q, Goat_q, Cabbage_q, Farmer_q);
endmodule
